# Fritzing sketch esquema (saved by Fritzing 0.9.3b)
breadboards: 1

parts:
  U1 = NodeMCU V1.0
  HC-SR04_Sensor_1 = HC-SR04 Ultrasonic Distance Sensor
  M2 = xy-mos d4184 [package=THT]
  M3 = DC Motor
  VCC1 = 4 x AAA Battery Mount

nets:
  GND: U1.GND, HC-SR04_Sensor_1.GND, M2.pin2, M2.pin6, M2.pin7, VCC1.-
  N1: U1.D5, M2.pin1, M2.pin3
  N2: U1.D6, HC-SR04_Sensor_1.TRIG
  N3: U1.D7, HC-SR04_Sensor_1.ECHO
  N4: HC-SR04_Sensor_1.VCC, M2.pin8, VCC1.+
  N5: M2.pin9, M3.pin_1
  N6: M2.pin10, M3.pin_2

notes:
  5V

custom parts:
  NodeMCU V1.0: ESP8266 based NodeMCU
  xy-mos d4184: xy-mos d4184 Two parallel N-Channel logic compatible MOSFETS with low Rds(on) for high current low-side switching applications.
